// Logisim project ALU.circ as structural Verilog: 7 circuits, main circuit multi
module multi (
  input  B0,
  input  B1,
  input  A0,
  input  A1,
  input  A2,
  input  B2,
  output R0,
  output R1,
  output R2,
  output R3,
  output S_R
);

  wire and_2_out, and_3_out, and_4_out, and_5_out, or_1_out, xor_1_out;

  xor xor_1 (xor_1_out, A2, B2);
  and and_1 (R0, B0, A0);
  and and_2 (and_2_out, B1, A0, A0);
  and and_3 (and_3_out, B0, A1);
  and and_4 (and_4_out, B1, A1);
  xor xor_2 (R1, and_2_out, and_3_out);
  and and_5 (and_5_out, and_2_out, and_3_out);
  xor xor_3 (R2, and_5_out, and_4_out);
  and and_6 (R3, and_5_out, and_4_out);
  or or_1 (or_1_out, R0, R1, R2, R3);
  and and_7 (S_R, xor_1_out, or_1_out);
endmodule

module add_sub (
  input  A2,
  input  B2,
  input  M,
  input  A0,
  input  B0,
  input  A1,
  input  B1,
  output R0,
  output R1,
  output Error,
  output S_Beff
);

  wire adder_1_cout, adder_1_out, adder_2_cout, adder_2_out, adder_3_cout, adder_3_out, adder_4_cout,
       adder_5_cout, adder_6_cout, adder_6_out, and_1_out, not_1_out, xor_2_out, xor_3_out, xor_4_out,
       xor_5_out, xor_6_out, xor_7_out, xor_8_out, xor_9_out;

  xor xor_1 (S_Beff, B2, M);
  xor xor_2 (xor_2_out, M, B2);
  xor xor_3 (xor_3_out, A2, xor_2_out);
  xor xor_4 (xor_4_out, xor_3_out, B0);
  xor xor_5 (xor_5_out, xor_3_out, B1);
  xor xor_6 (xor_6_out, 1'b0, xor_3_out);
  Adder #(.width(1)) adder_1 (.a(A0), .b(xor_4_out), .out(adder_1_out), .cin(xor_3_out), .cout(adder_1_cout));
  Adder #(.width(1)) adder_2 (.a(A1), .b(xor_5_out), .out(adder_2_out), .cin(adder_1_cout), .cout(adder_2_cout));
  Adder #(.width(1)) adder_3 (.a(1'b0), .b(xor_6_out), .out(adder_3_out), .cin(adder_2_cout), .cout(adder_3_cout));
  not not_1 (not_1_out, adder_3_cout);
  and and_1 (and_1_out, not_1_out, xor_3_out);
  xor xor_7 (xor_7_out, adder_1_out, and_1_out);
  xor xor_8 (xor_8_out, adder_2_out, and_1_out);
  xor xor_9 (xor_9_out, adder_3_out, and_1_out);
  Adder #(.width(1)) adder_4 (.a(1'b0), .b(xor_7_out), .out(R0), .cin(and_1_out), .cout(adder_4_cout));
  Adder #(.width(1)) adder_5 (.a(1'b0), .b(xor_8_out), .out(R1), .cin(adder_4_cout), .cout(adder_5_cout));
  Adder #(.width(1)) adder_6 (.a(xor_9_out), .b(1'b0), .out(adder_6_out), .cin(adder_5_cout), .cout(adder_6_cout));
  or or_1 (Error, adder_6_out, adder_6_cout);
endmodule

module comparator (
  input  M,
  input  A0,
  input  A1,
  input  A2,
  input  B2,
  input  B0,
  input  B1,
  output AGB,
  output EQ,
  output ALB,
  output Cout
);

  wire adder_1_cout, adder_1_out, adder_2_out, and_1_out, and_2_out, and_3_out, and_4_out, and_5_out,
       and_6_out, and_7_out, and_8_out, and_9_out, and_10_out, and_11_out, and_12_out, and_13_out,
       and_14_out, and_15_out, buffer_1_out, not_1_out, not_2_out, not_3_out, not_4_out, not_5_out,
       not_6_out, not_7_out, not_8_out, not_9_out, not_10_out, not_11_out, not_12_out, not_13_out,
       not_14_out, not_15_out, not_16_out, not_17_out, not_18_out, not_19_out, xnor_1_out, xnor_2_out,
       xnor_3_out;

  not not_1 (not_1_out, A0);
  not not_2 (not_2_out, A1);
  not not_3 (not_3_out, B0);
  not not_4 (not_4_out, B1);
  not not_5 (not_5_out, A2);
  and and_1 (and_1_out, not_1_out, not_2_out, not_3_out, not_4_out);
  xnor xnor_1 (xnor_1_out, B2, A2);
  not not_6 (not_6_out, B2);
  and and_2 (and_2_out, B2, not_5_out, not_5_out);
  not not_7 (not_7_out, B0);
  not not_8 (not_8_out, B1);
  and and_3 (and_3_out, not_6_out, A2);
  and and_4 (and_4_out, A2, B2);
  xnor xnor_2 (xnor_2_out, B2, A2);
  Adder #(.width(1)) adder_1 (.a(A0), .b(not_7_out), .out(adder_1_out), .cin(M), .cout(adder_1_cout));
  Adder #(.width(1)) adder_2 (.a(A1), .b(not_8_out), .out(adder_2_out), .cin(adder_1_cout), .cout(Cout));
  not not_9 (not_9_out, Cout);
  xnor xnor_3 (xnor_3_out, B2, A2);
  and and_5 (and_5_out, B2, A2);
  not not_10 (not_10_out, and_1_out);
  not not_11 (not_11_out, and_1_out);
  not not_12 (not_12_out, xnor_3_out);
  not not_13 (not_13_out, and_12_out);
  not not_14 (not_14_out, and_4_out);
  and and_6 (and_6_out, xnor_2_out, not_15_out, Cout);
  not not_15 (not_15_out, and_12_out);
  not not_16 (not_16_out, xnor_2_out);
  and and_7 (and_7_out, not_16_out, not_10_out, and_2_out);
  not not_17 (not_17_out, adder_1_out);
  not not_18 (not_18_out, adder_2_out);
  and and_8 (and_8_out, and_3_out, not_11_out, not_12_out);
  and and_9 (and_9_out, not_9_out, not_13_out, xnor_3_out);
  and and_10 (and_10_out, not_17_out, not_18_out);
  not not_19 (not_19_out, and_5_out);
  and and_11 (and_11_out, not_14_out, and_6_out);
  and and_12 (and_12_out, and_10_out, xnor_1_out, xnor_1_out);
  and and_13 (and_13_out, and_9_out, not_19_out);
  and and_14 (and_14_out, and_4_out, and_6_out);
  and and_15 (and_15_out, and_9_out, and_5_out);
  buf buffer_1 (buffer_1_out, and_12_out);
  or or_1 (ALB, and_8_out, and_13_out, and_14_out);
  or or_2 (AGB, and_11_out, and_15_out, and_7_out);
  or or_3 (EQ, and_1_out, buffer_1_out);
endmodule

module _1comp (
  input  A0,
  input  A1,
  input  A2,
  output R0,
  output R1,
  output R2
);

  not not_1 (R0, A0);
  not not_2 (R1, A1);
  not not_3 (R2, A2);
endmodule

module Decodeer (
  input  R3,
  input  R2,
  input  R1,
  input  R0,
  output A,
  output B,
  output C,
  output D,
  output E,
  output F,
  output G
);

  wire and_1_out, and_2_out, and_3_out, and_4_out, and_5_out, and_6_out, and_7_out, and_8_out, and_9_out,
       and_10_out, and_11_out, and_12_out, and_13_out, and_14_out, and_15_out, and_16_out, and_17_out,
       not_1_out, not_2_out, not_3_out, not_4_out, not_5_out, not_6_out, not_7_out, not_8_out, not_9_out,
       not_10_out, not_11_out, not_12_out, not_13_out, not_14_out, not_15_out, not_16_out, not_17_out,
       not_18_out, not_19_out, not_20_out, not_21_out, not_22_out;

  not not_1 (not_1_out, R2);
  and and_1 (and_1_out, not_1_out, not_2_out);
  not not_2 (not_2_out, R0);
  not not_3 (not_3_out, R2);
  and and_2 (and_2_out, not_3_out, R1);
  and and_3 (and_3_out, R2, R0);
  not not_4 (not_4_out, R2);
  not not_5 (not_5_out, R1);
  and and_4 (and_4_out, not_5_out, not_6_out);
  not not_6 (not_6_out, R0);
  and and_5 (and_5_out, R1, R0);
  not not_7 (not_7_out, R1);
  or or_1 (C, not_7_out, R0, R2);
  not not_8 (not_8_out, R2);
  and and_6 (and_6_out, not_8_out, not_9_out);
  not not_9 (not_9_out, R0);
  not not_10 (not_10_out, R2);
  and and_7 (and_7_out, not_10_out, R1);
  and and_8 (and_8_out, R1, not_11_out);
  not not_11 (not_11_out, R0);
  not not_12 (not_12_out, R1);
  and and_9 (and_9_out, R2, not_12_out, R0);
  not not_13 (not_13_out, R2);
  and and_10 (and_10_out, not_13_out, not_14_out);
  not not_14 (not_14_out, R0);
  and and_11 (and_11_out, R1, not_15_out);
  not not_15 (not_15_out, R0);
  not not_16 (not_16_out, R1);
  and and_12 (and_12_out, not_16_out, not_17_out);
  not not_17 (not_17_out, R0);
  and and_13 (and_13_out, R2, not_18_out);
  not not_18 (not_18_out, R1);
  and and_14 (and_14_out, R2, not_19_out);
  not not_19 (not_19_out, R0);
  not not_20 (not_20_out, R2);
  and and_15 (and_15_out, not_20_out, R1);
  and and_16 (and_16_out, R2, not_21_out);
  not not_21 (not_21_out, R1);
  and and_17 (and_17_out, R2, not_22_out);
  not not_22 (not_22_out, R0);
  or or_2 (A, and_1_out, and_2_out, and_3_out, R3);
  or or_3 (B, not_4_out, and_4_out, and_5_out);
  or or_4 (D, and_6_out, and_7_out, and_8_out, and_9_out);
  or or_5 (E, and_10_out, and_11_out);
  or or_6 (F, and_12_out, and_13_out, and_14_out, R3);
  or or_7 (G, and_15_out, and_16_out, and_17_out, R3);
endmodule

module sign_AS (
  input  A2,
  input  B_eff,
  input  NOT_ZERO,
  input  AGB,
  output R2
);

  wire and_1_out, and_2_out, and_3_out, not_1_out, not_2_out, or_1_out, xor_1_out;

  or or_1 (or_1_out, A2, xor_1_out);
  xor xor_1 (xor_1_out, B_eff, A2);
  not not_1 (not_1_out, xor_1_out);
  not not_2 (not_2_out, AGB);
  and and_1 (and_1_out, not_1_out, NOT_ZERO, A2);
  and and_2 (and_2_out, B_eff, xor_1_out, NOT_ZERO, or_1_out, not_2_out);
  and and_3 (and_3_out, or_1_out, xor_1_out, A2, NOT_ZERO, AGB);
  or or_2 (R2, and_1_out, and_2_out, and_3_out);
endmodule

module Full_System (
  input  B0,
  input  B1,
  input  B2,
  input  [2:0] in_4,
  input  A0,
  input  A1,
  input  A2
);

  wire add_sub_1_error, add_sub_1_r0, add_sub_1_r1, add_sub_1_s_beff, add_sub_2_error, add_sub_2_r0,
       add_sub_2_r1, add_sub_2_s_beff, comparator_1_agb, comparator_1_alb, comparator_1_cout,
       comparator_1_eq, decodeer_1_a, decodeer_1_b, decodeer_1_c, decodeer_1_d, decodeer_1_e, decodeer_1_f,
       decodeer_1_g, multi_1_r0, multi_1_r1, multi_1_r2, multi_1_r3, multi_1_s_r, multiplexer_1_out,
       multiplexer_2_out, multiplexer_3_out, multiplexer_4_out, multiplexer_5_out, multiplexer_6_out,
       n1comp_1_r0, n1comp_1_r1, n1comp_1_r2, or_1_out, or_2_out, sign_as_1_r2, sign_as_2_r2;

  multi multi_1 (
    .B0(B0), .B1(B1), .A0(A0), .A1(A1), .A2(A2), .B2(B2), .R0(multi_1_r0), .R1(multi_1_r1), .R2(multi_1_r2),
    .R3(multi_1_r3), .S_R(multi_1_s_r));
  comparator comparator_1 (
    .M(1'b1), .A0(A0), .A1(A1), .A2(A2), .B2(B2), .B0(B0), .B1(B1), .AGB(comparator_1_agb),
    .EQ(comparator_1_eq), .ALB(comparator_1_alb), .Cout(comparator_1_cout));
  sign_AS sign_as_1 (
    .A2(A2), .B_eff(add_sub_1_s_beff), .NOT_ZERO(or_1_out), .AGB(comparator_1_cout), .R2(sign_as_1_r2));
  add_sub add_sub_1 (
    .A2(A2), .B2(B2), .M(1'b1), .A0(A0), .B0(B0), .A1(A1), .B1(B1), .R0(add_sub_1_r0), .R1(add_sub_1_r1),
    .Error(add_sub_1_error), .S_Beff(add_sub_1_s_beff));
  sign_AS sign_as_2 (
    .A2(A2), .B_eff(add_sub_2_s_beff), .NOT_ZERO(or_2_out), .AGB(comparator_1_cout), .R2(sign_as_2_r2));
  add_sub add_sub_2 (
    .A2(A2), .B2(B2), .M(1'b0), .A0(A0), .B0(B0), .A1(A1), .B1(B1), .R0(add_sub_2_r0), .R1(add_sub_2_r1),
    .Error(add_sub_2_error), .S_Beff(add_sub_2_s_beff));
  _1comp u_1comp_1 (.A0(A0), .A1(A1), .A2(A2), .R0(n1comp_1_r0), .R1(n1comp_1_r1), .R2(n1comp_1_r2));
  or or_1 (or_1_out, add_sub_1_r0, add_sub_1_r1, add_sub_1_error);
  or or_2 (or_2_out, add_sub_2_r0, add_sub_2_r1, add_sub_2_error);
  Multiplexer #(.select(3), .disabled(0), .enable("false")) multiplexer_1 (
    .in0(sign_as_2_r2), .in1(sign_as_1_r2), .in2(multi_1_s_r), .in3(1'b0), .in4(n1comp_1_r2), .in5(1'b0),
    .in6(1'b0), .in7(1'b0), .out(multiplexer_1_out), .sel(in_4));
  Multiplexer #(.select(3), .disabled(0), .enable("false")) multiplexer_2 (
    .in0(add_sub_2_r0), .in1(add_sub_1_r0), .in2(multi_1_r0), .in3(comparator_1_agb), .in4(n1comp_1_r0),
    .in5(1'b0), .in6(1'b0), .in7(1'b0), .out(multiplexer_2_out), .sel(in_4));
  Multiplexer #(.select(3), .disabled(0), .enable("false")) multiplexer_3 (
    .in0(add_sub_2_r1), .in1(add_sub_1_r1), .in2(multi_1_r1), .in3(comparator_1_eq), .in4(n1comp_1_r1),
    .in5(1'b0), .in6(1'b0), .in7(1'b0), .out(multiplexer_3_out), .sel(in_4));
  Multiplexer #(.select(3), .disabled(0), .enable("false")) multiplexer_4 (
    .in0(add_sub_2_error), .in1(add_sub_1_error), .in2(multi_1_r2), .in3(comparator_1_alb), .in4(1'b0),
    .in5(1'b0), .in6(1'b0), .in7(1'b0), .out(multiplexer_4_out), .sel(in_4));
  Multiplexer #(.select(3), .disabled(0), .enable("false")) multiplexer_5 (
    .in0(1'b0), .in1(1'b0), .in2(multi_1_r3), .in3(1'b0), .in4(1'b0), .in5(1'b0), .in6(1'b0), .in7(1'b0),
    .out(multiplexer_5_out), .sel(in_4));
  Multiplexer #(.select(3), .disabled(0), .enable("false")) multiplexer_6 (
    .in0(add_sub_2_error), .in1(add_sub_1_error), .in2(1'b0), .in3(1'b0), .in4(1'b0), .in5(1'b0), .in6(1'b0),
    .in7(1'b0), .out(multiplexer_6_out), .sel(in_4));
  LED Sign (.in(multiplexer_1_out));
  LED Overflow (.in(multiplexer_6_out));
  Decodeer decodeer_1 (
    .R3(multiplexer_5_out), .R2(multiplexer_4_out), .R1(multiplexer_3_out), .R0(multiplexer_2_out),
    .A(decodeer_1_a), .B(decodeer_1_b), .C(decodeer_1_c), .D(decodeer_1_d), .E(decodeer_1_e),
    .F(decodeer_1_f), .G(decodeer_1_g));
  _7_Segment_Display u_7_segment_display_1 (
    .g(decodeer_1_g), .f(decodeer_1_f), .a(decodeer_1_a), .b(decodeer_1_b), .e(decodeer_1_e),
    .d(decodeer_1_d), .c(decodeer_1_c));  // open: dp
endmodule
